# Fritzing sketch serial_gateway (saved by Fritzing 0.9.3b)
circuit board: 4.91336cm x 4.56152cm

parts:
  Radio = NRF24L01+ Breakout Board
  Nano = Arduino Nano (Rev3.0)

nets:
  GND: Radio.GND, Nano.GND
  VCC: Radio.VCC, Nano.3V3
  N1: Radio.CE, Nano.D9
  N2: Radio.CS, Nano.D10
  N3: Radio.SCK, Nano.D13/SCK
  N4: Radio.MOSI, Nano.D11/MOSI
  N5: Radio.MISO, Nano.D12/MISO
